# Fritzing sketch Gassensor (saved by Fritzing 0.9.3b)
circuit board: 8.46667cm x 5.64444cm
breadboards: 1

parts:
  LCD1 = LCD screen
  Bauteil1 = Arduino Nano (Rev3.0)
  Bauteil2 = MQ-135 breakout  # not connected
  U1 = POT [package=pot_alpha_rv16af-20]

nets (from the breadboard view):
  VSS: LCD1.VSS, LCD1.R/W, LCD1.LED-, Bauteil1.GND, Bauteil1.D11/MOSI, U1.A
  VDD: LCD1.VDD, LCD1.LED+, Bauteil1.VIN, U1.E
  N1: LCD1.V0, U1.S
  N2: LCD1.RS, Bauteil1.D12/MISO
  N3: LCD1.DB4, Bauteil1.D5
  N4: LCD1.DB5, Bauteil1.D4
  N5: LCD1.DB6, Bauteil1.D3
  N6: LCD1.DB7, Bauteil1.D2

// code stored in the sketch: Untitled2.ino
#include <LiquidCrystal.h>

#define sensor	A0

LiquidCrystal lcd(12,11,5,4,3,2);

int gasLevel = 0;
String quality = "";

void setup() {
	Serial begin(9600);
	pinMode(sensor,INPUT);

	lcd.begin(16,2);
	lcd.setCursor(0,0);
	lcd.print("          ");
	lcd.setCursor(0,1);
	lcd.print("          ");
	lcd.setCursor(0,0);
	lcd.print(" Luft Sensor ");
	lcd.setCursor(0,1);
	lcd.print("Uff warme 120 s");
	delay(10000);
	lcd.setCursor(0,1);
	lcd.print("Uff warme 110 s");
	delay(10000);
	lcd.setCursor(0,1);
	lcd.print("Uff warme 100 s");
	delay(20000);
	lcd.setCursor(0,1);
	lcd.print("Uff warme 80 s ");
	delay(20000);
	lcd.setCursor(0,1);
	lcd.print("Uff warme 60 s ");
	delay(20000);
	lcd.setCursor(0,1);
	lcd.print("Uff warme 40 s ");
	delay(20000);
	lcd.setCursor(0,1);
	lcd.print("Uff warme 20 s ");
	delay(10000);
	lcd.setCursor(0,1);
	lcd.print("Uff warme 10 s ");
	delay(10000);
	lcd.setCursor(0,0);
	lcd.print("          ");
	lcd.setCursor(0,1);
	lcd.print("          ");
}

void loop() {
	gasLevel = analogRead(sensor);

	if(gasLevel<180) {
		quality = ":+    ";
	}
	else if(gasLevel>180 && gasLevel<225) {
		quality = ":+/-  ";
	}
	else if(gasLevel>225 && gasLevel<300) {
		quality = ":-    ";
	}
	else if(gasLevel>300) {
		quality = ":--   ";
	}

	lcd.setCursor (0,0);
	lcd.print("LuftQuali ist:");
	lcd.setCursor (0,1);
	lcd.print(gasLevel + quality);
	delay(500);
}
